// Logisim project ASSINGMENT DLD output (1).circ as structural Verilog: 1 circuit, main circuit main
module main (
  input  z,
  input  y,
  input  x,
  output A,
  output B,
  output C,
  output D,
  output E,
  output F,
  output G
);

  wire not_1_out, not_2_out, not_3_out, x_prime_z_prime_out, xy_prime_out, xy_prime_z_out, xz_out,
       xz_prime_out, yx_prime_out, yz_prime_out, z_prime_y_prime_out, zy_out;

  not not_1 (not_1_out, z);
  not not_2 (not_2_out, y);
  not not_3 (not_3_out, x);
  and zy (zy_out, z, y);
  and xz (xz_out, z, x);
  or u_a (A, xz_out, y, x_prime_z_prime_out);
  or u_b (B, z_prime_y_prime_out, xy_prime_out, xz_prime_out);
  or u_c (C, not_3_out, z_prime_y_prime_out, zy_out);
  or u_d (D, x_prime_z_prime_out, yz_prime_out);
  _7_Segment_Display u_7_segment_display_1 (.g(F), .f(B), .a(A), .b(C), .e(D), .d(G), .c(E));  // open: dp
  and yz_prime (yz_prime_out, y, not_1_out);
  or u_e (E, x, not_2_out, z);
  or u_f (F, yx_prime_out, xy_prime_out, xz_prime_out);
  and yx_prime (yx_prime_out, y, not_3_out);
  or u_g (G, x_prime_z_prime_out, yx_prime_out, yz_prime_out, xy_prime_z_out);
  and xz_prime (xz_prime_out, x, not_1_out);
  and xy_prime (xy_prime_out, x, not_2_out);
  and xy_prime_z (xy_prime_z_out, x, not_2_out, z);
  and z_prime_y_prime (z_prime_y_prime_out, not_2_out, not_1_out);
  and x_prime_z_prime (x_prime_z_prime_out, not_1_out, not_3_out);
endmodule
