// Logisim project ASSINGMENT DLD output (2).circ as structural Verilog: 1 circuit, main circuit main
module main (
  input  i1,
  input  i2,
  input  i3,
  input  i4,
  input  i5,
  input  i6,
  input  i7,
  output x,
  output y,
  output z
);

  wire xor_1_out, xor_2_out, xor_3_out, xor_4_out;

  xor xor_1 (xor_1_out, i1, i2);
  xor xor_2 (xor_2_out, i5, i6);
  xor xor_3 (xor_3_out, i3, i4);
  xor xor_4 (xor_4_out, i2, i4);
  or or_1 (z, i7, xor_2_out, xor_3_out, xor_1_out);
  or or_2 (y, xor_4_out, i6);

  assign x = i4;
endmodule
